// Logisim project p3.circ as structural Verilog: 14 circuits, main circuit main
module main (
  input  Reset
);

  wire alu_1_zero, ALUSrc, clock_1_out, control_1_branch, control_1_memread, control_1_memwrite,
       control_1_regdst, control_1_regwrite, ExtOp, MemtoReg;
  wire [1:0] alucontrol_1_aluop1, control_1_aluop, control_1_ol;
  wire [4:0] multiplexer_1_out;
  wire [29:0] imm16;
  wire [31:0] alu_1_result, dm_1_readdata, gpr_1_readdata1, gpr_1_readdata2, ifu_1_instruction,
       multiplexer_2_out, multiplexer_3_out;
  wire [31:30] ext_1_out;

  Clock clock_1 (.out(clock_1_out));
  // Probe on ifu_1_instruction
  IFU ifu_1 (
    .clk(clock_1_out), .IfBeq(control_1_branch), .imm16(imm16), .Zero(alu_1_zero),
    .Instruction(ifu_1_instruction), .Reset(Reset));
  // Probe on ifu_1_instruction[5:0]
  Control control_1 (
    .Op(ifu_1_instruction[31:26]), .RegDst(control_1_regdst), .ALUSrc(ALUSrc), .MemtoReg(MemtoReg),
    .RegWrite(control_1_regwrite), .MemRead(control_1_memread), .MemWrite(control_1_memwrite),
    .Branch(control_1_branch), .ALUOp(control_1_aluop), .ol(control_1_ol), .ExtOp(ExtOp));
  Multiplexer #(.width(5)) multiplexer_1 (
    .in0(ifu_1_instruction[20:16]), .in1(ifu_1_instruction[15:11]), .out(multiplexer_1_out),
    .sel(control_1_regdst));  // open: en
  GPR gpr_1 (
    .readRegister1(ifu_1_instruction[25:21]), .regWrite(control_1_regwrite), .writeData(multiplexer_3_out),
    .writeRegister(multiplexer_1_out), .readData1(gpr_1_readdata1), .readData2(gpr_1_readdata2),
    .readRegister2(ifu_1_instruction[20:16]), .clk(clock_1_out));
  EXT ext_1 (.ExtOp(ExtOp), .imm16(ifu_1_instruction[15:0]), .out({ext_1_out, imm16}));
  Multiplexer #(.width(32)) multiplexer_2 (
    .in0(gpr_1_readdata2), .in1({ext_1_out, imm16}), .out(multiplexer_2_out), .sel(ALUSrc));  // open: en
  ALUControl alucontrol_1 (
    .ol(control_1_ol), .ALUOp(control_1_aluop), .FuncL6(ifu_1_instruction[5:0]), .ALUOp1(alucontrol_1_aluop1));
  // Probe on alu_1_result
  ALU alu_1 (
    .ALUOp1(alucontrol_1_aluop1), .A(gpr_1_readdata1), .B(multiplexer_2_out), .Zero(alu_1_zero),
    .Result(alu_1_result));
  DM dm_1 (
    .Address(alu_1_result[4:0]), .Writedata(gpr_1_readdata2), .MemWrite(control_1_memwrite),
    .clk(clock_1_out), .MemRead(control_1_memread), .Readdata(dm_1_readdata));
  Multiplexer #(.width(32)) multiplexer_3 (
    .in0(alu_1_result), .in1(dm_1_readdata), .out(multiplexer_3_out), .sel(MemtoReg));  // open: en
  // Probe on dm_1_readdata

  // Notes on the sheet:
  //   Func
  //   RD
  //   Rt
  //   Rs
  //   ALUOp
  //   imm16
endmodule

// PC
module IFU (
  input  clk,
  input  Reset,
  input  IfBeq,
  input  [29:0] imm16,
  input  Zero,
  output [31:0] Instruction
);

  wire and_1_out;
  wire [29:0] adder_1_out, adder_2_out, multiplexer_1_out, PC_q;

  and and_1 (and_1_out, IfBeq, Zero);
  Multiplexer #(.width(30)) multiplexer_1 (
    .in0(adder_1_out), .in1(adder_2_out), .out(multiplexer_1_out), .sel(and_1_out));  // open: en
  Register #(.width(30)) PC (.D(multiplexer_1_out), .Q(PC_q), .clk(clk), .clr(Reset));  // open: en
  Adder #(.width(30)) adder_1 (.a(PC_q), .b(30'h1), .out(adder_1_out));  // open: cin, cout
  Adder #(.width(30)) adder_2 (.a(adder_1_out), .b(imm16), .out(adder_2_out));  // open: cin, cout
  ROM #(.addrWidth(5), .dataWidth(32)) rom_1 (.addr(PC_q[4:0]), .data(Instruction));  // open: sel

  // Notes on the sheet:
  //   contents of rom_1 (hex, n*v repeats v):
  //   3c010000 34280000 340c0000 358d000a 35890001 1895021 ad0a0000 1094021 1495021 1896021 118d0001
  //   118cfffa 8d0afff6 3c0b0003 16a5023 ad0a0000 1094021 1896023 11800001 118cfff8
endmodule

module GPR (
  input  [4:0] readRegister1,
  input  regWrite,
  input  [31:0] writeData,
  input  [4:0] writeRegister,
  input  clk,
  input  [4:0] readRegister2,
  output [31:0] readData1,
  output [31:0] readData2
);

  wire and_1_out, and_2_out, and_3_out, and_4_out, and_5_out, and_6_out, and_7_out, and_8_out, and_9_out,
       and_10_out, and_11_out, and_12_out, and_13_out, and_14_out, and_15_out, and_16_out, and_17_out,
       and_18_out, and_19_out, and_20_out, and_21_out, and_22_out, and_23_out, and_24_out, and_25_out,
       and_26_out, and_27_out, and_28_out, and_29_out, and_30_out, and_31_out, and_32_out, regist0, regist1,
       regist2, regist3, regist4, regist5, regist6, regist7, regist8, regist9, regist10, regist11, regist12,
       regist13, regist14, regist15, regist16, regist17, regist18, regist19, regist20, regist21, regist22,
       regist23, regist24, regist25, regist26, regist27, regist28, regist29, regist30, regist31;
  wire [31:0] register0, register1, register2, register3, register4, register5, register6, register7,
       register8, register9, register10, register11, register12, register13, register14, register15,
       register16, register17, register18, register19, register20, register21, register22, register23,
       register24, register25, register26, register27, register28, register29, register30, register31;

  Decoder #(.select(5)) decoder_1 (
    .out0(regist0), .out1(regist1), .out2(regist2), .out3(regist3), .out4(regist4), .out5(regist5),
    .out6(regist6), .out7(regist7), .out8(regist8), .out9(regist9), .out10(regist10), .out11(regist11),
    .out12(regist12), .out13(regist13), .out14(regist14), .out15(regist15), .out16(regist16),
    .out17(regist17), .out18(regist18), .out19(regist19), .out20(regist20), .out21(regist21),
    .out22(regist22), .out23(regist23), .out24(regist24), .out25(regist25), .out26(regist26),
    .out27(regist27), .out28(regist28), .out29(regist29), .out30(regist30), .out31(regist31),
    .sel(writeRegister));  // open: en
  and and_1 (and_1_out, regWrite, regist0);
  Register #(.width(32)) register_1 (.D(writeData), .en(and_1_out), .Q(register0), .clk(clk));  // open: clr
  and and_2 (and_2_out, regWrite, regist8);
  Register #(.width(32)) register_2 (.D(writeData), .en(and_2_out), .Q(register8), .clk(clk));  // open: clr
  and and_3 (and_3_out, regWrite, regist16);
  Register #(.width(32)) register_3 (.D(writeData), .en(and_3_out), .Q(register16), .clk(clk));  // open: clr
  and and_4 (and_4_out, regWrite, regist24);
  Register #(.width(32)) register_4 (.D(writeData), .en(and_4_out), .Q(register24), .clk(clk));  // open: clr
  and and_5 (and_5_out, regWrite, regist1);
  Register #(.width(32)) register_5 (.D(writeData), .en(and_5_out), .Q(register1), .clk(clk));  // open: clr
  and and_6 (and_6_out, regWrite, regist9);
  Register #(.width(32)) register_6 (.D(writeData), .en(and_6_out), .Q(register9), .clk(clk));  // open: clr
  and and_7 (and_7_out, regWrite, regist17);
  Register #(.width(32)) register_7 (.D(writeData), .en(and_7_out), .Q(register17), .clk(clk));  // open: clr
  and and_8 (and_8_out, regWrite, regist25);
  Register #(.width(32)) register_8 (.D(writeData), .en(and_8_out), .Q(register25), .clk(clk));  // open: clr
  and and_9 (and_9_out, regWrite, regist2);
  and and_10 (and_10_out, regWrite, regist10);
  and and_11 (and_11_out, regWrite, regist18);
  and and_12 (and_12_out, regWrite, regist26);
  and and_13 (and_13_out, regWrite, regist3);
  Register #(.width(32)) register_9 (.D(writeData), .en(and_9_out), .Q(register2), .clk(clk));  // open: clr
  and and_14 (and_14_out, regWrite, regist11);
  Register #(.width(32)) register_10 (.D(writeData), .en(and_10_out), .Q(register10), .clk(clk));  // open: clr
  and and_15 (and_15_out, regWrite, regist19);
  Register #(.width(32)) register_11 (.D(writeData), .en(and_11_out), .Q(register18), .clk(clk));  // open: clr
  and and_16 (and_16_out, regWrite, regist27);
  Register #(.width(32)) register_12 (.D(writeData), .en(and_12_out), .Q(register26), .clk(clk));  // open: clr
  and and_17 (and_17_out, regWrite, regist4);
  Register #(.width(32)) register_13 (.D(writeData), .en(and_13_out), .Q(register3), .clk(clk));  // open: clr
  and and_18 (and_18_out, regWrite, regist12);
  Register #(.width(32)) register_14 (.D(writeData), .en(and_14_out), .Q(register11), .clk(clk));  // open: clr
  and and_19 (and_19_out, regWrite, regist20);
  Register #(.width(32)) register_15 (.D(writeData), .en(and_15_out), .Q(register19), .clk(clk));  // open: clr
  and and_20 (and_20_out, regWrite, regist28);
  Register #(.width(32)) register_16 (.D(writeData), .en(and_16_out), .Q(register27), .clk(clk));  // open: clr
  buf and_21 (and_21_out, regist5);  // AND_Gate
  Register #(.width(32)) register_17 (.D(writeData), .en(and_17_out), .Q(register4), .clk(clk));  // open: clr
  and and_22 (and_22_out, regWrite, regist13);
  Register #(.width(32)) register_18 (.D(writeData), .en(and_18_out), .Q(register12), .clk(clk));  // open: clr
  and and_23 (and_23_out, regWrite, regist21);
  Register #(.width(32)) register_19 (.D(writeData), .en(and_19_out), .Q(register20), .clk(clk));  // open: clr
  and and_24 (and_24_out, regWrite, regist29);
  Register #(.width(32)) register_20 (.D(writeData), .en(and_20_out), .Q(register28), .clk(clk));  // open: clr
  Register #(.width(32)) register_21 (.D(writeData), .en(and_21_out), .Q(register5), .clk(clk));  // open: clr
  Register #(.width(32)) register_22 (.D(writeData), .en(and_22_out), .Q(register13), .clk(clk));  // open: clr
  Register #(.width(32)) register_23 (.D(writeData), .en(and_23_out), .Q(register21), .clk(clk));  // open: clr
  Register #(.width(32)) register_24 (.D(writeData), .en(and_24_out), .Q(register29), .clk(clk));  // open: clr
  and and_25 (and_25_out, regWrite, regist6);
  Register #(.width(32)) register_25 (.D(writeData), .en(and_25_out), .Q(register6), .clk(clk));  // open: clr
  and and_26 (and_26_out, regWrite, regist14);
  Register #(.width(32)) register_26 (.D(writeData), .en(and_26_out), .Q(register14), .clk(clk));  // open: clr
  and and_27 (and_27_out, regWrite, regist22);
  Register #(.width(32)) register_27 (.D(writeData), .en(and_27_out), .Q(register22), .clk(clk));  // open: clr
  and and_28 (and_28_out, regWrite, regist30);
  Register #(.width(32)) register_28 (.D(writeData), .en(and_28_out), .Q(register30), .clk(clk));  // open: clr
  and and_29 (and_29_out, regWrite, regist7);
  Register #(.width(32)) register_29 (.D(writeData), .en(and_29_out), .Q(register7), .clk(clk));  // open: clr
  and and_30 (and_30_out, regWrite, regist15);
  Register #(.width(32)) register_30 (.D(writeData), .en(and_30_out), .Q(register15), .clk(clk));  // open: clr
  and and_31 (and_31_out, regWrite, regist23);
  Register #(.width(32)) register_31 (.D(writeData), .en(and_31_out), .Q(register23), .clk(clk));  // open: clr
  and and_32 (and_32_out, regWrite, regist31);
  Register #(.width(32)) register_32 (.D(writeData), .en(and_32_out), .Q(register31), .clk(clk));  // open: clr
  Multiplexer #(.select(5), .width(32)) multiplexer_1 (
    .in0(register0), .in1(register1), .in2(register2), .in3(register3), .in4(register4), .in5(register5),
    .in6(register6), .in7(register7), .in8(register8), .in9(register9), .in10(register10), .in11(register11),
    .in12(register12), .in13(register13), .in14(register14), .in15(register15), .in16(register16),
    .in17(register17), .in18(register18), .in19(register19), .in20(register20), .in21(register21),
    .in22(register22), .in23(register23), .in24(register24), .in25(register25), .in26(register26),
    .in27(register27), .in28(register28), .in29(register29), .in30(register30), .in31(register31),
    .out(readData1), .sel(readRegister1));  // open: en
  Multiplexer #(.select(5), .width(32)) multiplexer_2 (
    .in0(register0), .in1(register1), .in2(register2), .in3(register3), .in4(register4), .in5(register5),
    .in6(register6), .in7(register7), .in8(register8), .in9(register9), .in10(register10), .in11(register11),
    .in12(register12), .in13(register13), .in14(register14), .in15(register15), .in16(register16),
    .in17(register17), .in18(register18), .in19(register19), .in20(register20), .in21(register21),
    .in22(register22), .in23(register23), .in24(register24), .in25(register25), .in26(register26),
    .in27(register27), .in28(register28), .in29(register29), .in30(register30), .in31(register31),
    .out(readData2), .sel(readRegister2));  // open: en
endmodule

module ALU (
  input  [1:0] ALUOp1,
  input  [31:0] A,
  input  [31:0] B,
  output Zero,
  output [31:0] Result
);

  wire or_2_out;
  wire [31:0] bit32adder_1_sum, or_1_out, sub_1_sub;

  bit32adder bit32adder_1 (.a(A), .b(B), .cin(1'b0), .sum(bit32adder_1_sum));  // open: cout
  sub sub_1 (.A(A), .B(B), .sub(sub_1_sub));
  assign or_1_out = A | B;  // OR_Gate or_1, 32 bits wide
  Multiplexer #(.select(2), .width(32)) multiplexer_1 (
    .in0(bit32adder_1_sum), .in1(sub_1_sub), .in2(or_1_out), .in3({B[15:0], {16{1'b0}}}), .out(Result),
    .sel(ALUOp1));  // open: en
  not not_1 (Zero, or_2_out);
  or or_2 (or_2_out, Result[0], Result[1], Result[2], Result[3], Result[4], Result[5], Result[6], Result[7], Result[8], Result[9], Result[10], Result[11], Result[12], Result[13], Result[14], Result[15], Result[17], Result[18], Result[19], Result[20], Result[21], Result[22], Result[23], Result[24], Result[25], Result[26], Result[27], Result[28], Result[29], Result[30], Result[31], Result[16]);
endmodule

module onebitadder (
  input  a,
  input  b,
  input  cin,
  output sum,
  output cout
);

  wire and_1_out, and_2_out, and_3_out, and_4_out, and_5_out, and_6_out, and_7_out, not_1_out, not_2_out,
       not_3_out, not_4_out, not_5_out, not_6_out;

  not not_1 (not_1_out, a);
  not not_2 (not_2_out, b);
  not not_3 (not_3_out, a);
  not not_4 (not_4_out, cin);
  not not_5 (not_5_out, b);
  not not_6 (not_6_out, cin);
  and and_1 (and_1_out, b, cin);
  and and_2 (and_2_out, a, cin);
  and and_3 (and_3_out, a, b);
  and and_4 (and_4_out, not_1_out, not_2_out, cin);
  and and_5 (and_5_out, not_3_out, b, not_4_out);
  and and_6 (and_6_out, a, not_5_out, not_6_out);
  and and_7 (and_7_out, a, b, cin);
  or or_1 (cout, and_1_out, and_2_out, and_3_out);
  or or_2 (sum, and_4_out, and_5_out, and_6_out, and_7_out);
endmodule

module fourbitadder (
  input  [3:0] a,
  input  cin,
  input  [3:0] b,
  output cout,
  output [3:0] sum
);

  wire onebitadder_2_cout, onebitadder_3_cout, onebitadder_4_cout;

  onebitadder onebitadder_1 (.a(b[3]), .b(a[3]), .cin(onebitadder_2_cout), .sum(sum[3]), .cout(cout));
  onebitadder onebitadder_2 (.a(b[2]), .b(a[2]), .cin(onebitadder_3_cout), .sum(sum[2]), .cout(onebitadder_2_cout));
  onebitadder onebitadder_3 (.a(b[1]), .b(a[1]), .cin(onebitadder_4_cout), .sum(sum[1]), .cout(onebitadder_3_cout));
  onebitadder onebitadder_4 (.a(b[0]), .b(a[0]), .cin(cin), .sum(sum[0]), .cout(onebitadder_4_cout));
endmodule

module eightbitadder (
  input  [7:0] a,
  input  cin,
  input  [7:0] b,
  output cout,
  output [7:0] sum
);

  wire fourbitadder_2_cout;

  fourbitadder fourbitadder_1 (.cout(cout), .a(a[7:4]), .b(b[7:4]), .cin(fourbitadder_2_cout), .sum(sum[7:4]));
  fourbitadder fourbitadder_2 (.cout(fourbitadder_2_cout), .a(a[3:0]), .b(b[3:0]), .cin(cin), .sum(sum[3:0]));
endmodule

module bit32adder (
  input  [31:0] a,
  input  cin,
  input  [31:0] b,
  output cout,
  output [31:0] sum
);

  wire eightbitadder_2_cout, eightbitadder_3_cout, eightbitadder_4_cout;

  eightbitadder eightbitadder_1 (.a(a[31:24]), .cout(cout), .b(b[31:24]), .cin(eightbitadder_3_cout), .sum(sum[31:24]));
  eightbitadder eightbitadder_2 (
    .a(a[15:8]), .cout(eightbitadder_2_cout), .b(b[15:8]), .cin(eightbitadder_4_cout), .sum(sum[15:8]));
  eightbitadder eightbitadder_3 (
    .a(a[23:16]), .cout(eightbitadder_3_cout), .b(b[23:16]), .cin(eightbitadder_2_cout), .sum(sum[23:16]));
  eightbitadder eightbitadder_4 (.a(a[7:0]), .cout(eightbitadder_4_cout), .b(b[7:0]), .cin(cin), .sum(sum[7:0]));
endmodule

module DM (
  input  [4:0] Address,
  input  [31:0] Writedata,
  input  MemWrite,
  input  MemRead,
  input  clk,
  output [31:0] Readdata
);

  RAM #(.addrWidth(5), .dataWidth(32), .bus("separate")) ram_1 (
    .addr(Address), .din(Writedata), .data(Readdata), .str(MemWrite), .clk(clk), .ld(MemRead));  // open: sel, clr
endmodule

module sub (
  input  [31:0] A,
  input  [31:0] B,
  output [31:0] sub
);

  wire bit32adder_2_cout;
  wire [31:0] bit32adder_1_sum, not_1_out;

  bit32adder bit32adder_1 (.a(not_1_out), .b(32'h1), .cin(1'b0), .sum(bit32adder_1_sum));  // open: cout
  assign not_1_out = ~B;  // NOT_Gate not_1, 32 bits wide
  bit32adder bit32adder_2 (.a(A), .b(bit32adder_1_sum), .cin(1'b0), .cout(bit32adder_2_cout), .sum(sub));
endmodule

module EXT (
  input  ExtOp,
  input  [15:0] imm16,
  output [31:0] out
);

  wire [31:0] bit_extender_1_out, bit_extender_2_out;

  assign bit_extender_1_out = {{16{1'b0}}, imm16};  // Bit_Extender bit_extender_1
  assign bit_extender_2_out = {{16{imm16[15]}}, imm16};  // Bit_Extender bit_extender_2
  Multiplexer #(.width(32)) multiplexer_1 (
    .in0(bit_extender_1_out), .in1(bit_extender_2_out), .out(out), .sel(ExtOp));  // open: en
endmodule

module Control (
  input  [5:0] Op,
  output RegDst,
  output ALUSrc,
  output MemtoReg,
  output RegWrite,
  output MemRead,
  output MemWrite,
  output Branch,
  output [1:0] ALUOp,
  output [1:0] ol,
  output ExtOp
);

  wire not_1_out, not_2_out, not_3_out, not_4_out, not_5_out, not_6_out, not_7_out, not_8_out, not_9_out,
       not_10_out, not_11_out, not_12_out, not_13_out, not_14_out, not_15_out, not_16_out, not_17_out,
       not_18_out, not_19_out, not_20_out, not_21_out;

  not not_1 (not_1_out, Op[4]);
  not not_2 (not_2_out, Op[1]);
  not not_3 (not_3_out, Op[3]);
  not not_4 (not_4_out, Op[0]);
  not not_5 (not_5_out, Op[2]);
  not not_6 (not_6_out, Op[5]);
  and R_Format (ALUOp[1], not_4_out, not_2_out, not_5_out, not_3_out, not_1_out, not_6_out);
  not not_7 (not_7_out, Op[4]);
  not not_8 (not_8_out, Op[2]);
  not not_9 (not_9_out, Op[3]);
  and lw (MemRead, Op[0], Op[1], not_8_out, not_9_out, not_7_out, Op[5]);
  not not_10 (not_10_out, Op[4]);
  not not_11 (not_11_out, Op[2]);
  and sw (MemWrite, Op[0], Op[1], not_11_out, Op[3], not_10_out, Op[5]);
  not not_12 (not_12_out, Op[1]);
  not not_13 (not_13_out, Op[4]);
  not not_14 (not_14_out, Op[5]);
  not not_15 (not_15_out, Op[0]);
  not not_16 (not_16_out, Op[3]);
  and beq (ALUOp[0], not_15_out, not_12_out, Op[2], not_16_out, not_13_out, not_14_out);
  not not_17 (not_17_out, Op[1]);
  not not_18 (not_18_out, Op[4]);
  and ori (ol[0], Op[0], not_17_out, Op[2], Op[3], not_18_out, not_19_out);
  not not_19 (not_19_out, Op[5]);
  and lui (ol[1], Op[0], Op[1], Op[2], Op[3], not_20_out, not_21_out);
  not not_20 (not_20_out, Op[4]);
  not not_21 (not_21_out, Op[5]);
  or or_1 (ALUSrc, MemRead, ol[0], ol[1], MemWrite);
  or or_2 (RegWrite, ALUOp[1], ol[1], ol[0], MemRead);
  or or_3 (ExtOp, MemWrite, MemRead);

  assign Branch = ALUOp[0];
  assign MemtoReg = MemRead;
  assign RegDst = ALUOp[1];
endmodule

module main1 (
  input  Reset
);

  wire alu_1_zero, ALUSrc, clock_1_out, control_1_branch, control_1_memread, control_1_memwrite,
       control_1_regdst, control_1_regwrite, MemtoReg, undriven, undriven_2;
  wire [1:0] control_1_aluop;
  wire [4:0] multiplexer_1_out;
  wire [31:0] alu_1_result, dm_1_readdata, ext_1_out, gpr_1_readdata1, gpr_1_readdata2, ifu_1_instruction,
       multiplexer_3_out;

  Clock clock_1 (.out(clock_1_out));
  IFU ifu_1 (
    .clk(clock_1_out), .IfBeq(control_1_branch), .Zero(alu_1_zero), .Instruction(ifu_1_instruction),
    .Reset(Reset));  // open: imm16
  Control control_1 (
    .Op(ifu_1_instruction[31:26]), .RegDst(control_1_regdst), .ALUSrc(ALUSrc), .MemtoReg(MemtoReg),
    .RegWrite(control_1_regwrite), .MemRead(control_1_memread), .MemWrite(control_1_memwrite),
    .Branch(control_1_branch), .ALUOp(control_1_aluop), .ExtOp(control_1_branch));  // open: ol
  // Probe on undriven
  // Probe on undriven_2
  Multiplexer #(.width(5)) multiplexer_1 (
    .in0(ifu_1_instruction[20:16]), .in1(ifu_1_instruction[15:11]), .out(multiplexer_1_out),
    .sel(control_1_regdst));  // open: en
  GPR gpr_1 (
    .readRegister1(ifu_1_instruction[25:21]), .regWrite(control_1_regwrite), .writeData(multiplexer_3_out),
    .writeRegister(multiplexer_1_out), .readData1(gpr_1_readdata1), .readData2(gpr_1_readdata2),
    .readRegister2(ifu_1_instruction[20:16]), .clk(clock_1_out));
  EXT ext_1 (.imm16(ifu_1_instruction[15:0]), .out(ext_1_out));  // open: ExtOp
  Multiplexer #(.width(32)) multiplexer_2 (.in0(gpr_1_readdata2), .in1(ext_1_out), .sel(ALUSrc));  // open: out, en
  ALU alu_1 (
    .ALUOp1(control_1_aluop), .A(gpr_1_readdata1), .B(gpr_1_readdata2), .Zero(alu_1_zero),
    .Result(alu_1_result));
  DM dm_1 (
    .Address(alu_1_result[4:0]), .Writedata(gpr_1_readdata2), .MemWrite(control_1_memwrite),
    .clk(clock_1_out), .MemRead(control_1_memread), .Readdata(dm_1_readdata));
  Multiplexer #(.width(32)) multiplexer_3 (
    .in0(alu_1_result), .in1(dm_1_readdata), .out(multiplexer_3_out), .sel(MemtoReg));  // open: en

  // Notes on the sheet:
  //   Func
  //   RD
  //   Rt
  //   Rs
  //   ALUOp
  //   imm16
endmodule

// ALUcon
module ALUControl (
  input  [1:0] ol,
  input  [1:0] ALUOp,
  input  [5:0] FuncL6,
  output [1:0] ALUOp1
);

  wire and_1_out, and_2_out, and_3_out, and_4_out, and_5_out, not_1_out, not_2_out, not_3_out, not_4_out,
       not_5_out, not_6_out, not_7_out, not_8_out;

  not not_1 (not_1_out, FuncL6[2]);
  not not_2 (not_2_out, FuncL6[3]);
  not not_3 (not_3_out, FuncL6[4]);
  not not_4 (not_4_out, ALUOp[0]);
  not not_5 (not_5_out, ALUOp[1]);
  not not_6 (not_6_out, ol[0]);
  not not_7 (not_7_out, ol[1]);
  not not_8 (not_8_out, ol[0]);
  and and_1 (and_1_out, FuncL6[0], FuncL6[1], not_1_out, not_2_out, not_3_out, FuncL6[5], ALUOp[1], not_4_out);
  and and_2 (and_2_out, not_5_out, ALUOp[0]);
  and and_3 (and_3_out, ol[1], not_6_out);
  and and_4 (and_4_out, not_7_out, ol[0]);
  and and_5 (and_5_out, ol[1], not_8_out);
  or or_1 (ALUOp1[1], and_4_out, and_5_out);
  or or_2 (ALUOp1[0], and_1_out, and_2_out, and_3_out);

  // Other names for the same wires on the sheet: a0 = ALUOp[0]; a1 = ALUOp[1]; Fun0 = FuncL6[0]; Fun1 = FuncL6[1];
  //   Fun2 = FuncL6[2]; Fun3 = FuncL6[3]; Fun4 = FuncL6[4]; Fun5 = FuncL6[5]; L0 = ol[0]; L1 = ol[1]
endmodule
